# Fritzing sketch MICRO_Adafruit_GPS_OLED_Multiscreen (saved by Fritzing 0.8.7b)
breadboards: 1

parts:
  ARDUINO1 = Arduino Micro
  GPS1 = Adafruit Ultimate GPS Breakout
  OLED1 = 128x64 Monochrom OLED Display with SPI Control
  LED1 = LED - 3mm [color="Red (633nm)" package="3 mm [THT]"]
  S3 = Pushbutton [package="[SMD]"]
  R4 = Resistor [package="0402 [SMD]"]

nets:
  N1: ARDUINO1.TX, GPS1.RX
  N2: ARDUINO1.RX, GPS1.TX
  N3: ARDUINO1.D4, LED1.anode
  N4: ARDUINO1.D5, S3.Pin_3, S3.Pin_4
  N5: ARDUINO1.D9, OLED1.Data
  N6: ARDUINO1.D10, OLED1.Clock
  N7: ARDUINO1.D11, OLED1.SA0/DC
  N8: ARDUINO1.D12, OLED1.CS
  N9: ARDUINO1.D13, OLED1.Reset
  VIN: ARDUINO1.5V, GPS1.VIN, OLED1.Vin
  GND: GPS1.GND, OLED1.GND, S3.Pin_1, S3.Pin_2, R4.Pin_0
  N10: LED1.cathode, R4.Pin_1

notes:
  Arduino MICRO, Adafruit's Ultimate GPS v3 and 128x64 OLED connected using SPI. The GPS serial interface uses hardware serial (serial1) on Micro. -- brycej 02/24/2014
  NOTE!: Switch uses INPUT_PULLUP removing the need for a resisitor.

custom parts:
  Arduino Micro: Arduino Micro Microcontroller
